# Fritzing sketch RAdar (saved by Fritzing 0.9.3b)
breadboards: 1

parts:
  Част1 = Arduino Nano (Rev3.0)
  J1 = Basic Servo
  hc-sr1 = hc-sr04

nets:
  N1: Част1.D10, hc-sr1.Trig
  N2: Част1.D11/MOSI, hc-sr1.Echo
  N3: Част1.D12/MISO, J1.pulse
  GND: Част1.GND, J1.gnd, hc-sr1.GND
  VCC: Част1.5V, J1.vcc, hc-sr1.VCC

notes:
  ATASAV
